# Fritzing sketch fritzing (saved by Fritzing 0.9.3b)
breadboards: 2

parts:
  Mod1 = Raspberry Pi Pico
  JP1 = Header 4 [package=jst-4-pth]
  LED1 = RGB LED (com. cathode, rgb) [package="5 mm [THT]"]
  U1 = LIPO-110mAh [package=lipo-110]
  J1 = Piezo Speaker

nets:
  N1: Mod1.pin_3, Mod1.pin_8, Mod1.pin_13, Mod1.pin_28, Mod1.pin_33, Mod1.pin_38, Mod1.pin_42, JP1.3, U1.-, J1.pin1
  N2: Mod1.pin_6, JP1.1
  N3: Mod1.pin_7, JP1.2
  N4: Mod1.pin_14, LED1.blue_anode
  N5: Mod1.pin_15, LED1.green_anode
  N6: Mod1.pin_16, LED1.common_cathode
  N7: Mod1.pin_17, J1.pin2
  N8: JP1.4, LED1.red_anode, U1.+

notes:
  DFRobot HuskyLens AI Camera

custom parts:
  Raspberry Pi Pico: Raspberry Pi Pico. Based around the RP2040 microcontroller the Pico is a low cost microcontroller device bringing Raspberry Pi quality, cost, and easy of use to the microcontroller space. Jan 2021, Split part in to two versions: tht (this one) and SMD. This one will drill holes for a .1 in header in pcb to allow plugging in the module as well as providing pads to solder the module to the top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
